// Logisim project monocicloredux.circ as structural Verilog: 6 circuits, main circuit main
module main (
  input  in_1
);

  wire BGWE, BRANCH, BRANCHJUMP, button_1_out, CLK, IMMJUMP, IMMTYPE, ITYPE, JAL, MEMWE, or_1_out, SUB;
  wire [1:0] DATA, ENDRBorIMM2BITS, multiplexer_5_out;
  wire [2:0] OP;
  wire [3:0] bit_extender_1_out, multiplexer_4_out;
  wire [3:2] IMM4BITS;
  wire [7:0] dual_port_ram_1_data, IMM, multiplexer_1_out, multiplexer_2_out, multiplexer_3_out,
       multiplexer_6_out, multiplexer_7_out, PCPLUS, RA, RB, register_1_q, ula_1_s0;
  wire [7:4] inst;

  Multiplexer #(.width(8)) multiplexer_1 (.in0(8'h1), .in1(IMM), .out(multiplexer_1_out), .sel(IMMJUMP));
  Adder adder_1 (.a(register_1_q), .b(multiplexer_1_out), .out(PCPLUS), .cin(1'b0));  // open: cout
  Multiplexer #(.width(8)) multiplexer_2 (.in0(PCPLUS), .in1(RB), .out(multiplexer_2_out), .sel(or_1_out));
  or or_1 (or_1_out, BRANCHJUMP, JAL);
  Register register_1 (.D(multiplexer_2_out), .en(1'b1), .clk(CLK), .Q(register_1_q), .clr(button_1_out));
  Clock #(.highDuration(2), .lowDuration(2)) clock_1 (.out(CLK));
  Button button_1 (.out(button_1_out));
  Multiplexer #(.width(8)) multiplexer_3 (
    .in0({inst, IMM4BITS, ENDRBorIMM2BITS}), .in1(RA), .out(multiplexer_3_out), .sel(MEMWE));
  ROM #(.addrWidth(4), .dataWidth(13)) UC (
    .addr(inst), .data({DATA, IMMJUMP, BRANCH, MEMWE, BGWE, IMMTYPE, ITYPE, SUB, JAL, OP}));
  dual_port_ram dual_port_ram_1 (
    .addr(RB), .pc(register_1_q), .d(multiplexer_3_out), .w(MEMWE),
    .instr({inst, IMM4BITS, ENDRBorIMM2BITS}), .data(dual_port_ram_1_data));
  assign bit_extender_1_out = {{2{ENDRBorIMM2BITS[1]}}, ENDRBorIMM2BITS};  // Bit_Extender bit_extender_1
  Multiplexer #(.width(4)) multiplexer_4 (
    .in0(bit_extender_1_out), .in1({IMM4BITS, ENDRBorIMM2BITS}), .out(multiplexer_4_out), .sel(IMMTYPE));
  assign IMM = {{4{multiplexer_4_out[3]}}, multiplexer_4_out};  // Bit_Extender bit_extender_2
  Multiplexer #(.width(2)) multiplexer_5 (.in0(IMM4BITS), .in1(2'b00), .out(multiplexer_5_out), .sel(IMMTYPE));
  Multiplexer #(.select(2), .width(8)) multiplexer_6 (
    .in0(dual_port_ram_1_data), .in1(PCPLUS), .in2(ula_1_s0), .out(multiplexer_6_out), .sel(DATA));  // open: in3
  BG bg_1 (
    .CLK(CLK), .BGWE(BGWE), .RA(multiplexer_5_out), .RB(ENDRBorIMM2BITS), .DATA(multiplexer_6_out), .S0(RA),
    .S1(RB));
  Multiplexer #(.width(8)) multiplexer_7 (.in0(RB), .in1(IMM), .out(multiplexer_7_out), .sel(ITYPE));
  ULA ula_1 (.A(RA), .B(multiplexer_7_out), .SUB(SUB), .OPERATION(OP), .OVERFLOW(in_1), .s0(ula_1_s0));
  branchctrl branchctrl_1 (.RA(RA), .branch(BRANCH), .bjump(BRANCHJUMP));

  // Other names for the same wires on the sheet: IMM4BITS[1:0] = ENDRBorIMM2BITS;
  //   inst[3:0] = {IMM4BITS, ENDRBorIMM2BITS}; OPCODE[3:0] = inst

  // Notes on the sheet:
  //   contents of UC (hex, n*v repeats v):
  //   202 462 82 102 10e0 10e7 10a0 88a 1086 1081 1082 1083 1080 1090 1084 1085
endmodule

module dual_port_ram (
  input  [7:0] addr,
  input  [7:0] pc,
  input  [7:0] d,
  input  w,
  output [7:0] instr,
  output [7:0] data
);

  wire clock_1_out, or_1_out;
  wire [7:0] multiplexer_1_out;

  Clock #(.highDuration(2), .lowDuration(2)) clock_1 (.out(clock_1_out));
  or or_1 (or_1_out, w, clock_1_out);
  Multiplexer #(.width(8)) multiplexer_1 (.in0(addr), .in1(pc), .out(multiplexer_1_out), .sel(clock_1_out));
  RAM #(.asyncread("true")) ram_1 (
    .addr(multiplexer_1_out), .we(or_1_out), .oe(1'b1), .clk(clock_1_out), .din(d), .dout(data));
  Register #(.trigger("falling")) pcbuf (.D(data), .en(1'b1), .clk(clock_1_out), .Q(instr));  // open: clr
endmodule

module ULA (
  input  [7:0] A,
  input  [7:0] B,
  input  SUB,
  input  [2:0] OPERATION,
  output OVERFLOW,
  output [7:0] s0
);

  wire [7:0] adder_1_out, adder_2_out, and_1_out, multiplexer_1_out, not_1_out, not_2_out, or_1_out,
       shifter_1_out, shifter_2_out, xor_1_out;

  assign not_1_out = ~B;  // NOT_Gate not_1, 8 bits wide
  Multiplexer #(.width(8)) multiplexer_1 (.in0(B), .in1(adder_1_out), .out(multiplexer_1_out), .sel(SUB));
  Adder adder_1 (.a(not_1_out), .b(8'h1), .out(adder_1_out));  // open: cin, cout
  Adder adder_2 (.a(A), .b(multiplexer_1_out), .out(adder_2_out));  // open: cin, cout
  assign and_1_out = A & B;  // AND_Gate and_1, 8 bits wide
  assign or_1_out = A | B;  // OR_Gate or_1, 8 bits wide
  assign xor_1_out = A ^ B;  // XOR_Gate xor_1, 8 bits wide
  Shifter shifter_1 (.in(A), .\dist (B[2:0]), .out(shifter_1_out));
  Shifter #(.shift("lr")) shifter_2 (.in(A), .\dist (B[2:0]), .out(shifter_2_out));
  assign not_2_out = ~B;  // NOT_Gate not_2, 8 bits wide
  SUMOverflow sumoverflow_1 (.A(A[7]), .B(B[7]), .OP(OPERATION), .S(adder_2_out[7]), .OVERFLOW(OVERFLOW));
  Multiplexer #(.select(3), .width(8)) multiplexer_2 (
    .in0(adder_2_out), .in1(and_1_out), .in2(or_1_out), .in3(xor_1_out), .in4(shifter_1_out),
    .in5(shifter_2_out), .in6(not_2_out), .in7({B[3:0], A[3:0]}), .out(s0), .sel(OPERATION));

  // Other names for the same wires on the sheet: OP[2:0] = OPERATION
endmodule

module SUMOverflow (
  input  A,
  input  B,
  input  [2:0] OP,
  input  S,
  output OVERFLOW
);

  wire xnor_1_out, xor_1_out;

  xnor xnor_1 (xnor_1_out, A, B);
  xor xor_1 (xor_1_out, B, S);
  and and_1 (OVERFLOW, xnor_1_out, xor_1_out, ~OP[0], ~OP[1], ~OP[2]);  // AND_Gate
endmodule

module BG (
  input  CLK,
  input  BGWE,
  input  [1:0] RA,
  input  [1:0] RB,
  input  [7:0] DATA,
  output [7:0] S0,
  output [7:0] S1
);

  wire CLK_t, demultiplexer_1_out0, demultiplexer_1_out1, demultiplexer_1_out2, demultiplexer_1_out3;
  wire [7:0] R0_q, R1_q, R2_q, R3_q;

  Clock #(.highDuration(2), .lowDuration(2)) clock_1 (.out(CLK_t));
  Demultiplexer #(.select(2)) demultiplexer_1 (
    .out0(demultiplexer_1_out0), .out1(demultiplexer_1_out1), .out2(demultiplexer_1_out2),
    .out3(demultiplexer_1_out3), .in(BGWE), .sel(RA));
  Register R0 (.D(DATA), .en(demultiplexer_1_out0), .clk(CLK_t), .Q(R0_q));  // open: clr
  Register R1 (.D(DATA), .en(demultiplexer_1_out1), .clk(CLK_t), .Q(R1_q));  // open: clr
  Register R2 (.D(DATA), .en(demultiplexer_1_out2), .clk(CLK_t), .Q(R2_q));  // open: clr
  Register R3 (.D(DATA), .en(demultiplexer_1_out3), .clk(CLK_t), .Q(R3_q));  // open: clr
  Multiplexer #(.select(2), .width(8)) multiplexer_1 (
    .in0(R0_q), .in1(R1_q), .in2(R2_q), .in3(R3_q), .out(S0), .sel(RA));
  Multiplexer #(.select(2), .width(8)) multiplexer_2 (
    .in0(R0_q), .in1(R1_q), .in2(R2_q), .in3(R3_q), .out(S1), .sel(RB));
endmodule

module branchctrl (
  input  [7:0] RA,
  input  branch,
  output bjump
);

  wire nor_1_out;

  nor nor_1 (nor_1_out, RA[0], RA[1], RA[2], RA[3], RA[4], RA[5], RA[6], RA[7]);
  and and_1 (bjump, nor_1_out, branch);
endmodule
